// Logisim project TD1.circ as structural Verilog
module Half_adder (
  input  A,
  input  B,
  output Sum,
  output C
);

  and and_1 (C, A, B);
  xor xor_1 (Sum, A, B);
endmodule

module Full_adder (
  input  C_in,
  input  A,
  input  B,
  output Sum,
  output C_out
);

  wire half_adder_1_c, half_adder_1_sum, half_adder_2_c;

  Half_adder half_adder_1 (.A(A), .B(B), .C(half_adder_1_c), .Sum(half_adder_1_sum));
  or or_1 (C_out, half_adder_1_c, half_adder_2_c);
  Half_adder half_adder_2 (.A(C_in), .B(half_adder_1_sum), .C(half_adder_2_c), .Sum(Sum));
endmodule

// +
module _4_bits_Full_adder (
  input  [3:0] in_1,
  input  [3:0] in_2,
  output Z,
  output [3:0] Sum,
  output V,
  output N,
  output out_7
);

  wire full_adder_1_c_out, full_adder_2_c_out, full_adder_3_c_out;

  Full_adder full_adder_1 (.A(in_1[0]), .B(in_2[0]), .C_in(1'b0), .C_out(full_adder_1_c_out), .Sum(Sum[0]));
  Full_adder full_adder_2 (
    .A(in_1[1]), .B(in_2[1]), .C_in(full_adder_1_c_out), .C_out(full_adder_2_c_out), .Sum(Sum[1]));
  Full_adder full_adder_3 (
    .A(in_1[2]), .B(in_2[2]), .C_in(full_adder_2_c_out), .C_out(full_adder_3_c_out), .Sum(Sum[2]));
  Full_adder full_adder_4 (.A(in_1[3]), .B(in_2[3]), .C_in(full_adder_3_c_out), .C_out(out_7), .Sum(Sum[3]));
  xor xor_1 (V, full_adder_3_c_out, out_7);
  and and_1 (Z, ~Sum[0], ~Sum[1], ~Sum[2], ~Sum[3], out_7);  // AND_Gate
  and and_2 (N, ~V, Sum[3]);  // AND_Gate
endmodule

module Light (
  input  On,
  input  Off,
  output Lampe
);

  wire and_1_out;

  and and_1 (and_1_out, ~Off, Lampe);  // AND_Gate
  or or_1 (Lampe, On, and_1_out);
endmodule

// -
module _4_bits_Soustractor (
  input  [3:0] A,
  input  [3:0] B,
  output Z,
  output [3:0] Sum,
  output V,
  output N,
  output C
);

  wire n4_bits_full_adder_1_v, n4_bits_full_adder_2_n, n4_bits_full_adder_2_v;
  wire [3:0] n4_bits_full_adder_1_sum, not_1_out;

  assign not_1_out = ~B;  // NOT_Gate not_1, 4 bits wide
  _4_bits_Full_adder u_4_bits_full_adder_1 (
    .in_1(not_1_out), .in_2(4'b0001), .Sum(n4_bits_full_adder_1_sum), .V(n4_bits_full_adder_1_v));  // open: out_7, Z, N
  _4_bits_Full_adder u_4_bits_full_adder_2 (
    .in_1(A), .in_2(n4_bits_full_adder_1_sum), .out_7(C), .Z(Z), .Sum(Sum), .V(n4_bits_full_adder_2_v),
    .N(n4_bits_full_adder_2_n));
  or or_1 (V, n4_bits_full_adder_2_v, n4_bits_full_adder_1_v);
  and and_1 (N, ~V, n4_bits_full_adder_2_n);  // AND_Gate
endmodule

module _4_bits_UAL (
  input  [1:0] F,
  input  [3:0] A,
  input  [3:0] B,
  output [3:0] R,
  output V,
  output N,
  output C
);

  wire [3:0] demultiplexer_1_out0, demultiplexer_1_out1, demultiplexer_1_out2, demultiplexer_1_out3,
       demultiplexer_2_out0, demultiplexer_2_out1, demultiplexer_2_out2, demultiplexer_2_out3;

  Demultiplexer #(.select(2), .width(4), .enable("false")) demultiplexer_1 (
    .out0(demultiplexer_1_out0), .out1(demultiplexer_1_out1), .out2(demultiplexer_1_out2),
    .out3(demultiplexer_1_out3), .in(A), .sel(F));
  Demultiplexer #(.select(2), .width(4), .enable("false")) demultiplexer_2 (
    .out0(demultiplexer_2_out0), .out1(demultiplexer_2_out1), .out2(demultiplexer_2_out2),
    .out3(demultiplexer_2_out3), .in(B), .sel(F));
  _4_bits_Full_adder u_4_bits_full_adder_1 (
    .in_1(demultiplexer_1_out2), .in_2(demultiplexer_2_out2));  // open: out_7, Z, Sum, V, N
  _4_bits_Soustractor u_4_bits_soustractor_1 (
    .A(demultiplexer_1_out3), .B(demultiplexer_2_out3));  // open: C, Z, Sum, V, N
  // OR_Gate or_1 has open pins: in0=demultiplexer_1_out0, in1=demultiplexer_2_out0, out=open
  // AND_Gate and_1 has open pins: in0=demultiplexer_1_out1, in1=demultiplexer_2_out1, out=open
endmodule
